// Logisim project ALU_design1.circ as structural Verilog: 1 circuit, main circuit ALU_design1
module ALU_design1 (
  input  in_1,
  input  in_2,
  input  in_3,
  input  in_4,
  input  in_5,
  input  in_6,
  input  in_7,
  input  in_8,
  input  in_9,
  input  [1:0] in_10,
  input  in_11,
  output out_12,
  output out_13,
  output out_14,
  output out_15,
  output out_16,
  output out_17,
  output out_18
);

  wire buffer_1_out, buffer_2_out, buffer_3_out, buffer_4_out, decoder_1_out1, decoder_1_out2,
       decoder_1_out3, n4_bit_full_adder_1_out_10, n4_bit_full_adder_1_out_11, n4_bit_full_adder_1_out_12,
       n4_bit_full_adder_1_out_13, n4_bit_full_adder_1_out_14, nandxorcontrollogic_1_out_10,
       nandxorcontrollogic_1_out_11, nandxorcontrollogic_1_out_12, nandxorcontrollogic_1_out_13, not_1_out,
       shift_rotate_register_1_out_8, shift_rotate_register_1_out_9, shift_rotate_register_1_out_10,
       shift_rotate_register_1_out_11, shift_rotate_register_1_out_12;

  Decoder #(.select(2), .disabled(0), .enable("false")) decoder_1 (
    .out1(decoder_1_out1), .out2(decoder_1_out2), .out3(decoder_1_out3), .sel(in_10));  // open: out0
  NandXorControlLogic nandxorcontrollogic_1 (
    .in_9(in_9), .in_1(in_1), .in_2(in_2), .in_3(in_3), .in_4(in_4), .in_5(in_5), .in_6(in_6), .in_7(in_7),
    .in_8(in_8), .out_10(nandxorcontrollogic_1_out_10), .out_11(nandxorcontrollogic_1_out_11),
    .out_12(nandxorcontrollogic_1_out_12), .out_13(nandxorcontrollogic_1_out_13));
  not not_1 (not_1_out, decoder_1_out3);
  assign out_16 = decoder_1_out1 ? n4_bit_full_adder_1_out_11 : 1'bz;  // Controlled_Buffer controlled_buffer_1
  assign out_14 = decoder_1_out1 ? n4_bit_full_adder_1_out_10 : 1'bz;  // Controlled_Buffer controlled_buffer_2
  assign out_17 = decoder_1_out1 ? n4_bit_full_adder_1_out_12 : 1'bz;  // Controlled_Buffer controlled_buffer_3
  assign out_14 = decoder_1_out2 ? nandxorcontrollogic_1_out_10 : 1'bz;  // Controlled_Buffer controlled_buffer_4
  Shift_Rotate_Register shift_rotate_register_1 (
    .in_5(in_11), .in_7(not_1_out), .in_6(in_9), .in_1(in_1), .in_2(in_2), .in_3(in_3), .in_4(in_4),
    .out_9(shift_rotate_register_1_out_9), .out_10(shift_rotate_register_1_out_10),
    .out_11(shift_rotate_register_1_out_11), .out_12(shift_rotate_register_1_out_12),
    .out_8(shift_rotate_register_1_out_8));
  assign out_18 = decoder_1_out1 ? n4_bit_full_adder_1_out_13 : 1'bz;  // Controlled_Buffer controlled_buffer_5
  assign out_17 = decoder_1_out2 ? nandxorcontrollogic_1_out_12 : 1'bz;  // Controlled_Buffer controlled_buffer_6
  assign out_18 = decoder_1_out2 ? nandxorcontrollogic_1_out_13 : 1'bz;  // Controlled_Buffer controlled_buffer_7
  assign out_16 = decoder_1_out2 ? nandxorcontrollogic_1_out_11 : 1'bz;  // Controlled_Buffer controlled_buffer_8
  assign out_16 = decoder_1_out3 ? shift_rotate_register_1_out_10 : 1'bz;  // Controlled_Buffer controlled_buffer_9
  assign out_18 = decoder_1_out3 ? shift_rotate_register_1_out_12 : 1'bz;  // Controlled_Buffer controlled_buffer_10
  assign out_14 = decoder_1_out3 ? shift_rotate_register_1_out_9 : 1'bz;  // Controlled_Buffer controlled_buffer_11
  assign out_17 = decoder_1_out3 ? shift_rotate_register_1_out_11 : 1'bz;  // Controlled_Buffer controlled_buffer_12
  _4_bit_Full_adder u_4_bit_full_adder_1 (
    .in_9(in_9), .out_14(n4_bit_full_adder_1_out_14), .in_5(in_1), .in_6(in_2), .in_7(in_3), .in_8(in_4),
    .in_1(in_5), .in_2(in_6), .in_3(in_7), .in_4(in_8), .out_10(n4_bit_full_adder_1_out_10),
    .out_11(n4_bit_full_adder_1_out_11), .out_12(n4_bit_full_adder_1_out_12),
    .out_13(n4_bit_full_adder_1_out_13));
  assign out_12 = decoder_1_out1 ? n4_bit_full_adder_1_out_14 : 1'bz;  // Controlled_Buffer controlled_buffer_13
  assign out_12 = decoder_1_out3 ? shift_rotate_register_1_out_8 : 1'bz;  // Controlled_Buffer controlled_buffer_14
  buf buffer_1 (buffer_1_out, out_18);
  Pull_Resistor pull_resistor_1 (.node(buffer_1_out));
  buf buffer_2 (buffer_2_out, out_17);
  buf buffer_3 (buffer_3_out, out_16);
  Pull_Resistor pull_resistor_2 (.node(buffer_3_out));
  buf buffer_4 (buffer_4_out, out_14);
  Pull_Resistor pull_resistor_3 (.node(buffer_2_out));
  Pull_Resistor pull_resistor_4 (.node(buffer_4_out));
  nor nor_1 (out_13, buffer_1_out, buffer_2_out, buffer_3_out, buffer_4_out);

  assign out_15 = out_14;
endmodule
