// Logisim project Architecture without control unit.circ as structural Verilog: 1 circuit, main circuit Architecture1
module Architecture1 (
  input  in_1,
  input  in_2,
  input  in_3,
  input  in_4,
  input  in_5,
  input  in_6,
  input  in_7,
  input  in_8,
  input  in_9,
  input  in_10,
  input  in_11,
  input  [1:0] in_12,
  input  in_13,
  input  in_14,
  input  in_15,
  input  in_16,
  input  in_17,
  input  in_18,
  input  in_19,
  input  in_20,
  input  in_21,
  input  in_22,
  input  in_23,
  output out_24,
  output out_25,
  output out_26,
  output out_27,
  output N,
  output Z,
  output C,
  output out_31,
  output out_32,
  output out_33,
  output out_34,
  output out_35,
  output out_36,
  output out_37,
  output out_38,
  output out_39
);

  wire clock_1_out, or_1_out, program_counter_1_p1, program_counter_1_p5, program_counter_1_p9,
       program_counter_1_p12, pull_resistor_7_node, R1_p5, R1_p10, R1_p13, R1_p15, R2_p5, R2_p10, R2_p13,
       R2_p15, R3_p5, R3_p10, R3_p13, R3_p15, R4_p5, R4_p10, R4_p13, R4_p15;
  wire [3:0] R1_p12;

  Clock clock_1 (.out(clock_1_out));
  // General_Purpose_Register R1: pin names not known; wires that end beside it: in_13, clock_1_out, in_14, R1_p12[3], R1_p5, R1_p12[3], R1_p12[2], R1_p12[2], R1_p12[1], R1_p10, R1_p12[1], R1_p12[0], R1_p13, R1_p12[0], R1_p15
  LED led_1 (.in(R1_p5));
  // General_Purpose_Register R3: pin names not known; wires that end beside it: in_20, clock_1_out, in_21, R1_p12[3], R3_p5, R1_p12[3], R1_p12[2], R1_p12[2], R1_p12[1], R3_p10, R1_p12[1], R1_p12[0], R3_p13, R1_p12[0], R3_p15
  LED led_2 (.in(R3_p5));
  LED led_3 (.in(R1_p10));
  LED led_4 (.in(R1_p13));
  LED led_5 (.in(R1_p15));
  LED led_6 (.in(R3_p10));
  LED led_7 (.in(R3_p15));
  LED led_8 (.in(R3_p13));
  // General_Purpose_Register R2: pin names not known; wires that end beside it: in_17, clock_1_out, in_19, R1_p12[3], R2_p5, R1_p12[3], R1_p12[2], R1_p12[2], R1_p12[1], R2_p10, R1_p12[1], R1_p12[0], R2_p13, R1_p12[0], R2_p15
  // General_Purpose_Register R4: pin names not known; wires that end beside it: in_22, clock_1_out, in_23, R1_p12[3], R4_p5, R1_p12[3], R1_p12[2], R1_p12[2], R1_p12[1], R4_p10, R1_p12[1], R1_p12[0], R4_p13, R1_p12[0], R4_p15
  LED led_9 (.in(R2_p5));
  LED led_10 (.in(R2_p13));
  LED led_11 (.in(R2_p10));
  LED led_12 (.in(R4_p5));
  LED led_13 (.in(R4_p10));
  LED led_14 (.in(R4_p13));
  LED led_15 (.in(R2_p15));
  LED led_16 (.in(R4_p15));
  // RAM_ROM_with_MAR ram_rom_with_mar_1: pin names not known; wires that end beside it: in_4, clock_1_out, in_5, in_6, in_8, in_10, R1_p12, R1_p12, R1_p12[0], R1_p12[1], R1_p12[2], R1_p12[3]
  LED led_17 (.in(R1_p12[3]));
  LED led_18 (.in(R1_p12[2]));
  Pull_Resistor pull_resistor_1 (.node(R1_p12[2]));
  Pull_Resistor pull_resistor_2 (.node(R1_p12[3]));
  LED led_19 (.in(R1_p12[1]));
  LED led_20 (.in(R1_p12[0]));
  Pull_Resistor pull_resistor_3 (.node(R1_p12[1]));
  Pull_Resistor pull_resistor_4 (.node(R1_p12[0]));
  // Program_counter program_counter_1: pin names not known; wires that end beside it: program_counter_1_p1, R1_p12[3], R1_p12[3], R1_p12[2], program_counter_1_p5, R1_p12[2], R1_p12[1], R1_p12[1], program_counter_1_p9, R1_p12[0], R1_p12[0], program_counter_1_p12, in_1, in_2, in_3, clock_1_out
  LED led_21 (.in(program_counter_1_p1));
  LED led_22 (.in(program_counter_1_p5));
  LED led_23 (.in(program_counter_1_p12));
  LED led_24 (.in(program_counter_1_p9));
  // ALU_with_controls alu_with_controls_1: pin names not known; wires that end beside it: R1_p12[3], R1_p12[2], R1_p12[1], R1_p12[0], R1_p12[3], R1_p12[2], R1_p12[1], R1_p12[3], R1_p12[0], R1_p12[2], R1_p12[1], R1_p12[0], in_7, in_9, clock_1_out, in_11, in_12, out_24, out_25, out_26, out_27
  // Instruction_Register instruction_register_1: pin names not known; wires that end beside it: R1_p12[3], R1_p12[2], R1_p12[1], R1_p12[0], R1_p12[3], R1_p12[2], R1_p12[1], R1_p12[0], out_32, out_33, out_34, out_35, out_36, out_37, out_38, out_39, in_15, in_16, clock_1_out, in_18
  or or_1 (or_1_out, in_12[0], in_12[1]);
  Pull_Resistor pull_resistor_5 (.node(out_27));
  Pull_Resistor pull_resistor_6 (.node(out_25));
  Pull_Resistor pull_resistor_7 (.node(pull_resistor_7_node));
  // General_Purpose_Register Status_Register: pin names not known; wires that end beside it: or_1_out, clock_1_out, 1'b1, out_27, N, out_26, Z, out_25, C, pull_resistor_7_node, out_31

  // Notes on the sheet:
  //   R1
  //   R3
  //   R2
  //   R4
  //   Status Register
endmodule
