// Logisim project CPU_Architecture.circ as structural Verilog: 1 circuit, main circuit Architecture1
module Architecture1 (
  input  in_1,
  input  A3_in,
  input  A2_in,
  input  A1_in,
  input  A0_in,
  input  Clk,
  output A3_out,
  output A2_out,
  output A1_out,
  output A0_out,
  output MARin,
  output RAM_EN,
  output Data_in_bar___Data_out,
  output ROM1_out,
  output ROM2_out
);

  wire alu_with_controls_1_out_15, alu_with_controls_1_out_16, alu_with_controls_1_out_17,
       alu_with_controls_1_out_18, and_1_out, and_2_out, controlled_buffer_1_out, controlled_buffer_2_out,
       controlled_buffer_3_out, controlled_buffer_4_out, instruction_register_1_out_14,
       instruction_register_1_out_15, instruction_register_1_out_16, instruction_register_1_out_17,
       instruction_register_1_out_18, instruction_register_1_out_19, instruction_register_1_out_20,
       instruction_register_1_out_21, main_1_lsbin, main_1_msbin, main_1_out_16, main_1_out_18,
       main_1_out_21, main_1_out_23, main_1_out_26, main_1_out_28, main_1_out_31, main_1_pcclken,
       main_1_pcout, main_1_r1in, main_1_r2in, main_1_r3in, main_1_r3out, main_1_r4out, main_1_yin,
       not_1_out, or_1_out, or_2_out, or_3_out, program_counter_1_out_10, program_counter_1_out_11,
       program_counter_1_out_12, program_counter_1_out_13, pull_resistor_7_node, R1_out_9, R1_out_10,
       R1_out_11, R1_out_12, R2_out_9, R2_out_10, R2_out_11, R2_out_12, R3_out_9, R3_out_10, R3_out_11,
       R3_out_12, R4_out_9, R4_out_10, R4_out_11, R4_out_12, Status_Register_out_13, Status_Register_out_14,
       Status_Register_out_15, Status_Register_out_16;
  wire [1:0] main_1_out_33;

  and and_1 (and_1_out, RAM_EN, Data_in_bar___Data_out);
  assign controlled_buffer_1_out = or_1_out ? A3_in : 1'bz;  // Controlled_Buffer controlled_buffer_1
  assign controlled_buffer_2_out = or_1_out ? A2_in : 1'bz;  // Controlled_Buffer controlled_buffer_2
  assign controlled_buffer_3_out = or_1_out ? A1_in : 1'bz;  // Controlled_Buffer controlled_buffer_3
  assign controlled_buffer_4_out = or_1_out ? A0_in : 1'bz;  // Controlled_Buffer controlled_buffer_4
  or or_1 (or_1_out, ROM2_out, ROM1_out, and_1_out);
  General_Purpose_Register R1 (
    .in_5(main_1_r1in), .in_6(Clk), .in_8(main_1_out_16), .in_1(controlled_buffer_1_out),
    .in_2(controlled_buffer_2_out), .in_3(controlled_buffer_3_out), .in_4(controlled_buffer_4_out),
    .out_13(controlled_buffer_1_out), .out_14(controlled_buffer_2_out), .out_15(controlled_buffer_3_out),
    .out_16(controlled_buffer_4_out), .out_9(R1_out_9), .out_10(R1_out_10), .out_11(R1_out_11),
    .out_12(R1_out_12), .in_7(in_1));
  LED led_1 (.in(R1_out_9));
  General_Purpose_Register R3 (
    .in_5(main_1_r3in), .in_6(Clk), .in_8(main_1_r3out), .in_1(controlled_buffer_1_out),
    .in_2(controlled_buffer_2_out), .in_3(controlled_buffer_3_out), .in_4(controlled_buffer_4_out),
    .out_13(controlled_buffer_1_out), .out_14(controlled_buffer_2_out), .out_15(controlled_buffer_3_out),
    .out_16(controlled_buffer_4_out), .out_9(R3_out_9), .out_10(R3_out_10), .out_11(R3_out_11),
    .out_12(R3_out_12), .in_7(in_1));
  LED led_2 (.in(R3_out_9));
  LED led_3 (.in(R1_out_11));
  LED led_4 (.in(R1_out_10));
  LED led_5 (.in(R1_out_12));
  LED led_6 (.in(R3_out_12));
  LED led_7 (.in(R3_out_11));
  LED led_8 (.in(R3_out_10));
  not not_1 (not_1_out, Data_in_bar___Data_out);
  General_Purpose_Register R2 (
    .in_5(main_1_r2in), .in_6(Clk), .in_8(main_1_out_18), .in_1(controlled_buffer_1_out),
    .in_2(controlled_buffer_2_out), .in_3(controlled_buffer_3_out), .in_4(controlled_buffer_4_out),
    .out_13(controlled_buffer_1_out), .out_14(controlled_buffer_2_out), .out_15(controlled_buffer_3_out),
    .out_16(controlled_buffer_4_out), .out_9(R2_out_9), .out_10(R2_out_10), .out_11(R2_out_11),
    .out_12(R2_out_12), .in_7(in_1));
  General_Purpose_Register R4 (
    .in_5(main_1_out_21), .in_6(Clk), .in_8(main_1_r4out), .in_1(controlled_buffer_1_out),
    .in_2(controlled_buffer_2_out), .in_3(controlled_buffer_3_out), .in_4(controlled_buffer_4_out),
    .out_13(controlled_buffer_1_out), .out_14(controlled_buffer_2_out), .out_15(controlled_buffer_3_out),
    .out_16(controlled_buffer_4_out), .out_9(R4_out_9), .out_10(R4_out_10), .out_11(R4_out_11),
    .out_12(R4_out_12), .in_7(in_1));
  and and_2 (and_2_out, RAM_EN, not_1_out);
  LED led_9 (.in(R2_out_11));
  LED led_10 (.in(R2_out_10));
  LED led_11 (.in(R2_out_9));
  LED led_12 (.in(R4_out_9));
  LED led_13 (.in(R4_out_10));
  LED led_14 (.in(R4_out_11));
  or or_2 (or_2_out, MARin, and_2_out);
  LED led_15 (.in(R2_out_12));
  LED led_16 (.in(R4_out_12));
  assign A3_out = or_2_out ? controlled_buffer_1_out : 1'bz;  // Controlled_Buffer controlled_buffer_5
  assign A2_out = or_2_out ? controlled_buffer_2_out : 1'bz;  // Controlled_Buffer controlled_buffer_6
  assign A1_out = or_2_out ? controlled_buffer_3_out : 1'bz;  // Controlled_Buffer controlled_buffer_7
  assign A0_out = or_2_out ? controlled_buffer_4_out : 1'bz;  // Controlled_Buffer controlled_buffer_8
  LED led_17 (.in(controlled_buffer_1_out));
  LED led_18 (.in(controlled_buffer_2_out));
  Pull_Resistor pull_resistor_1 (.node(controlled_buffer_2_out));
  Pull_Resistor pull_resistor_2 (.node(controlled_buffer_1_out));
  LED led_19 (.in(controlled_buffer_3_out));
  LED led_20 (.in(controlled_buffer_4_out));
  Pull_Resistor pull_resistor_3 (.node(controlled_buffer_4_out));
  Pull_Resistor pull_resistor_4 (.node(controlled_buffer_3_out));
  Program_counter program_counter_1 (
    .in_1(controlled_buffer_1_out), .in_2(controlled_buffer_2_out), .in_3(controlled_buffer_3_out),
    .in_4(controlled_buffer_4_out), .out_14(controlled_buffer_1_out), .out_15(controlled_buffer_2_out),
    .out_16(controlled_buffer_3_out), .out_17(controlled_buffer_4_out), .in_5(main_1_out_23),
    .in_9(main_1_pcout), .in_7(main_1_pcclken), .in_6(Clk), .out_10(program_counter_1_out_10),
    .out_11(program_counter_1_out_11), .out_12(program_counter_1_out_12), .out_13(program_counter_1_out_13),
    .in_8(in_1));
  LED led_21 (.in(program_counter_1_out_10));
  LED led_22 (.in(program_counter_1_out_11));
  LED led_23 (.in(instruction_register_1_out_14));
  LED led_24 (.in(program_counter_1_out_13));
  LED led_25 (.in(program_counter_1_out_12));
  ALU_with_controls alu_with_controls_1 (
    .in_11(main_1_out_26), .in_12(Clk), .in_6(controlled_buffer_1_out), .in_7(controlled_buffer_2_out),
    .in_8(controlled_buffer_3_out), .in_9(controlled_buffer_4_out), .in_1(controlled_buffer_1_out),
    .in_2(controlled_buffer_2_out), .in_3(controlled_buffer_3_out), .in_4(controlled_buffer_4_out),
    .out_19(controlled_buffer_1_out), .out_20(controlled_buffer_2_out), .out_21(controlled_buffer_3_out),
    .out_22(controlled_buffer_4_out), .in_13(main_1_out_28), .in_14(main_1_out_33),
    .out_16(alu_with_controls_1_out_16), .out_17(alu_with_controls_1_out_17),
    .out_18(alu_with_controls_1_out_18), .in_5(main_1_yin), .out_15(alu_with_controls_1_out_15), .in_10(in_1));
  Instruction_Register instruction_register_1 (
    .in_1(controlled_buffer_1_out), .in_2(controlled_buffer_2_out), .in_3(controlled_buffer_3_out),
    .in_4(controlled_buffer_4_out), .in_6(main_1_msbin), .in_7(main_1_lsbin), .in_8(Clk),
    .out_18(instruction_register_1_out_18), .out_19(instruction_register_1_out_19),
    .out_20(instruction_register_1_out_20), .out_21(instruction_register_1_out_21),
    .out_17(instruction_register_1_out_17), .out_16(instruction_register_1_out_16),
    .out_15(instruction_register_1_out_15), .out_14(instruction_register_1_out_14), .in_9(main_1_out_31),
    .out_10(controlled_buffer_1_out), .out_11(controlled_buffer_2_out), .out_12(controlled_buffer_3_out),
    .out_13(controlled_buffer_4_out), .in_5(in_1));
  LED led_26 (.in(instruction_register_1_out_16));
  LED led_27 (.in(instruction_register_1_out_15));
  LED led_28 (.in(instruction_register_1_out_17));
  LED led_29 (.in(instruction_register_1_out_18));
  LED led_30 (.in(instruction_register_1_out_19));
  LED led_31 (.in(instruction_register_1_out_21));
  LED led_32 (.in(instruction_register_1_out_20));
  Control_logic_main main_1 (
    .in_9(Clk), .in_10(alu_with_controls_1_out_15), .in_11(Status_Register_out_13),
    .in_12(Status_Register_out_14), .in_14(Status_Register_out_15), .in_1(instruction_register_1_out_14),
    .in_2(instruction_register_1_out_15), .in_3(instruction_register_1_out_16),
    .in_4(instruction_register_1_out_17), .in_5(instruction_register_1_out_18),
    .in_6(instruction_register_1_out_19), .in_7(instruction_register_1_out_20),
    .in_8(instruction_register_1_out_21), .MARin(MARin), .out_35(RAM_EN), .RAMData(Data_in_bar___Data_out),
    .out_37(ROM1_out), .ROM2out(ROM2_out), .R1in(main_1_r1in), .out_16(main_1_out_16), .R2in(main_1_r2in),
    .out_18(main_1_out_18), .R3in(main_1_r3in), .R3out(main_1_r3out), .out_21(main_1_out_21),
    .R4out(main_1_r4out), .out_23(main_1_out_23), .PCClkEN(main_1_pcclken), .PCout(main_1_pcout),
    .out_26(main_1_out_26), .Yin(main_1_yin), .out_28(main_1_out_28), .MSBin(main_1_msbin),
    .LSBin(main_1_lsbin), .out_31(main_1_out_31), .DO1(main_1_out_33[1]), .out_33(main_1_out_33[0]),
    .in_13(in_1));
  LED led_33 (.in(alu_with_controls_1_out_16));
  LED led_34 (.in(alu_with_controls_1_out_17));
  LED led_35 (.in(alu_with_controls_1_out_18));
  LED led_36 (.in(alu_with_controls_1_out_15));
  or or_3 (or_3_out, main_1_out_33[0], main_1_out_33[1]);
  Pull_Resistor pull_resistor_5 (.node(alu_with_controls_1_out_18));
  Pull_Resistor pull_resistor_6 (.node(alu_with_controls_1_out_16));
  Pull_Resistor pull_resistor_7 (.node(pull_resistor_7_node));
  General_Purpose_Register Status_Register (
    .in_5(or_3_out), .in_6(Clk), .in_8(1'b1), .in_1(alu_with_controls_1_out_18),
    .in_2(alu_with_controls_1_out_17), .in_3(alu_with_controls_1_out_16), .in_4(pull_resistor_7_node),
    .out_13(Status_Register_out_13), .out_14(Status_Register_out_14), .out_15(Status_Register_out_15),
    .out_16(Status_Register_out_16), .in_7(in_1));  // open: out_9, out_10, out_11, out_12
  LED led_37 (.in(Status_Register_out_14));
  LED led_38 (.in(Status_Register_out_13));
  LED led_39 (.in(Status_Register_out_15));
  LED led_40 (.in(Status_Register_out_16));

  // Notes on the sheet:
  //   R1
  //   R3
  //   R2
  //   R4
  //   Status Register
  //   N
  //   Z
  //   C
endmodule
