// Logisim project Control logic.circ as structural Verilog
module main (
  input  in_1,
  input  in_2,
  input  in_3,
  input  in_4,
  input  in_5,
  input  in_6,
  input  in_7,
  input  in_8,
  input  in_9,
  input  in_10,
  input  in_11,
  input  in_12,
  input  in_13,
  input  in_14,
  output R1in,
  output out_16,
  output R2in,
  output out_18,
  output R3in,
  output R3out,
  output out_21,
  output R4out,
  output out_23,
  output PCClkEN,
  output PCout,
  output out_26,
  output Yin,
  output out_28,
  output MSBin,
  output LSBin,
  output out_31,
  output DO1,
  output out_33,
  output MARin,
  output out_35,
  output RAMData,
  output out_37,
  output ROM2out
);

  wire and_1_out, con_clk_3_1_x, lowercounter_1_out_5, lowercounter_1_out_6, not_1_out, uppercounter_1_out_4,
       uppercounter_1_out_5;

  not not_1 (not_1_out, in_9);
  Pull_Resistor pull_resistor_1 (.node(MARin));
  UpperCounter uppercounter_1 (
    .C(con_clk_3_1_x), .in_3(not_1_out), .out_4(uppercounter_1_out_4), .out_5(uppercounter_1_out_5),
    .in_2(in_13));
  Pull_Resistor pull_resistor_2 (.node(RAMData));
  Pull_Resistor pull_resistor_3 (.node(out_35));
  and and_1 (and_1_out, uppercounter_1_out_4, uppercounter_1_out_5);
  Pull_Resistor pull_resistor_4 (.node(out_37));
  Pull_Resistor pull_resistor_5 (.node(ROM2out));
  LowerCounter lowercounter_1 (
    .C(con_clk_3_1_x), .D(and_1_out), .in_3(not_1_out), .out_6(lowercounter_1_out_6),
    .out_5(lowercounter_1_out_5), .in_4(in_13));
  Con_Clk_3 con_clk_3_1 (
    .SC(in_10), .A(in_1), .B(in_2), .C(in_3), .D(in_4), .E(lowercounter_1_out_6), .F(lowercounter_1_out_5),
    .X(con_clk_3_1_x));
  Pull_Resistor pull_resistor_6 (.node(out_16));
  Pull_Resistor pull_resistor_7 (.node(R1in));
  Pull_Resistor pull_resistor_8 (.node(R2in));
  Pull_Resistor pull_resistor_9 (.node(out_18));
  Pull_Resistor pull_resistor_10 (.node(R3in));
  Pull_Resistor pull_resistor_11 (.node(R3out));
  Control_unit_internal control_unit_internal_1 (
    .in_13(in_11), .in_14(in_12), .in_15(in_14), .in_1(uppercounter_1_out_4), .in_2(uppercounter_1_out_5),
    .in_3(lowercounter_1_out_6), .in_4(lowercounter_1_out_5), .in_5(in_1), .in_6(in_2), .in_7(in_3),
    .in_8(in_4), .in_9(in_5), .in_10(in_6), .in_11(in_7), .in_12(in_8), .MARin(MARin), .out_17(out_35),
    .RAMData(RAMData), .out_19(out_37), .ROM2out(ROM2out), .R1in(R1in), .out_22(out_16), .R2in(R2in),
    .out_24(out_18), .R3in(R3in), .R3out(R3out), .out_27(out_21), .R4out(R4out), .out_29(out_23),
    .PCClkEN(PCClkEN), .PCout(PCout), .Xin(out_26), .Yin(Yin), .out_34(out_28), .MSBin(MSBin), .LSBin(LSBin),
    .out_37(out_31), .DO1(DO1), .out_39(out_33));
  Pull_Resistor pull_resistor_12 (.node(out_21));
  Pull_Resistor pull_resistor_13 (.node(out_23));
  Pull_Resistor pull_resistor_14 (.node(R4out));
  Pull_Resistor pull_resistor_15 (.node(PCClkEN));
  Pull_Resistor pull_resistor_16 (.node(PCout));
  Pull_Resistor pull_resistor_17 (.node(out_26));
  Pull_Resistor pull_resistor_18 (.node(Yin));
  Pull_Resistor pull_resistor_19 (.node(MSBin));
  Pull_Resistor pull_resistor_20 (.node(out_28));
  Pull_Resistor pull_resistor_21 (.node(LSBin));
  Pull_Resistor pull_resistor_22 (.node(out_31));
  Pull_Resistor pull_resistor_23 (.node(DO1));
  Pull_Resistor pull_resistor_24 (.node(out_33));

  // Notes on the sheet:
  //   RAMEN
  //   ROM1out
  //   R1out
  //   R2out
  //   R4in
  //   PCLoad
  //   Xin
  //   Alt
  //   LSBout
  //   DO0
endmodule

module UpperCounter (
  input  C,
  input  in_2,
  input  in_3,
  output out_4,
  output out_5
);

  wire and_1_out, and_2_out, and_3_out, and_4_out, not_1_out, not_2_out, not_3_out, not_4_out, not_5_out,
       or_1_out, or_2_out;

  D_Flip_Flop d_ff_1 (.clk(in_3), .D(or_1_out), .Q(out_4), .reset(in_2));  // open: Qn, preset, en
  not not_1 (not_1_out, out_4);
  not not_2 (not_2_out, out_5);
  not not_3 (not_3_out, C);
  not not_4 (not_4_out, C);
  and and_1 (and_1_out, not_1_out, out_5);
  and and_2 (and_2_out, out_4, not_2_out);
  and and_3 (and_3_out, out_4, not_3_out);
  not not_5 (not_5_out, out_5);
  and and_4 (and_4_out, out_4, not_4_out);
  D_Flip_Flop d_ff_2 (.clk(in_3), .D(or_2_out), .Q(out_5), .reset(in_2));  // open: Qn, preset, en
  or or_1 (or_1_out, and_1_out, and_2_out, and_3_out);
  or or_2 (or_2_out, not_5_out, and_4_out);
endmodule

module LowerCounter (
  input  C,
  input  D,
  input  in_3,
  input  in_4,
  output out_5,
  output out_6
);

  wire and_1_out, and_2_out, and_3_out, and_4_out, not_1_out, not_2_out, not_3_out, not_4_out, not_5_out,
       or_1_out, or_2_out;

  D_Flip_Flop d_ff_1 (.clk(in_3), .D(or_1_out), .Q(out_6), .reset(in_4));  // open: Qn, preset, en
  not not_1 (not_1_out, C);
  not not_2 (not_2_out, C);
  not not_3 (not_3_out, out_5);
  not not_4 (not_4_out, C);
  not not_5 (not_5_out, C);
  and and_1 (and_1_out, out_5, not_1_out, D);
  and and_2 (and_2_out, out_6, not_2_out, D);
  and and_3 (and_3_out, not_3_out, not_4_out, D);
  and and_4 (and_4_out, out_6, not_5_out, D);
  D_Flip_Flop d_ff_2 (.clk(in_3), .D(or_2_out), .Q(out_5), .reset(in_4));  // open: Qn, preset, en
  or or_1 (or_1_out, and_1_out, and_2_out);
  or or_2 (or_2_out, and_3_out, and_4_out);
endmodule

module Control_unit_internal (
  input  in_1,
  input  in_2,
  input  in_3,
  input  in_4,
  input  in_5,
  input  in_6,
  input  in_7,
  input  in_8,
  input  in_9,
  input  in_10,
  input  in_11,
  input  in_12,
  input  in_13,
  input  in_14,
  input  in_15,
  output MARin,
  output out_17,
  output RAMData,
  output out_19,
  output ROM2out,
  output R1in,
  output out_22,
  output R2in,
  output out_24,
  output R3in,
  output R3out,
  output out_27,
  output R4out,
  output out_29,
  output PCClkEN,
  output PCout,
  output Xin,
  output Yin,
  output out_34,
  output MSBin,
  output LSBin,
  output out_37,
  output DO1,
  output out_39
);

  RAMEN_C ramen_c_1 (.A(in_1), .X(out_17), .B(in_2), .C(in_3), .D(in_4), .E(in_5), .F(in_6), .G(in_7), .H(in_8));
  MARin_C marin_c_1 (.A(in_1), .B(in_2), .C(in_3), .D(in_4), .E(in_5), .F(in_6), .G(in_7), .H(in_8), .X(MARin));
  Pull_Resistor pull_resistor_1 (.node(out_17));
  Pull_Resistor pull_resistor_2 (.node(MARin));
  RAMData ramdata_1 (.A(in_1), .B(in_2), .C(in_3), .D(in_4), .E(in_5), .F(in_6), .G(in_7), .H(in_8), .X(RAMData));
  Pull_Resistor pull_resistor_3 (.node(RAMData));
  ROM1out rom1out_1 (.A(in_1), .B(in_2), .C(in_3), .D(in_4), .X(out_19));
  ROM2out rom2out_1 (.A(in_1), .B(in_2), .C(in_3), .D(in_4), .X(ROM2out));
  Pull_Resistor pull_resistor_4 (.node(out_19));
  Pull_Resistor pull_resistor_5 (.node(ROM2out));
  Reg_Control reg_control_1 (
    .A(in_1), .B(in_2), .C(in_3), .D(in_4), .E(in_5), .F(in_6), .G(in_7), .H(in_8), .P(in_9), .Q(in_10),
    .R(in_11), .S(in_12), .R1in(R1in), .R1out(out_22), .R2in(R2in), .R2out(out_24), .R3in(R3in),
    .R3out(R3out), .R4in(out_27), .R4out(R4out));
  Pull_Resistor pull_resistor_6 (.node(R1in));
  Pull_Resistor pull_resistor_7 (.node(out_22));
  Pull_Resistor pull_resistor_8 (.node(R2in));
  Pull_Resistor pull_resistor_9 (.node(R3in));
  Pull_Resistor pull_resistor_10 (.node(out_24));
  Pull_Resistor pull_resistor_11 (.node(R3out));
  Pull_Resistor pull_resistor_12 (.node(R4out));
  Pull_Resistor pull_resistor_13 (.node(out_27));
  PCLoad pcload_1 (
    .A(in_1), .B(in_2), .C(in_3), .D(in_4), .E(in_5), .F(in_6), .G(in_7), .H(in_8), .C0(in_15), .Z0(in_14),
    .N0(in_13), .X(out_29));
  Pull_Resistor pull_resistor_14 (.node(out_29));
  PCClkEN pcclken_1 (
    .A(in_1), .B(in_2), .C(in_3), .D(in_4), .E(in_5), .F(in_6), .G(in_7), .H(in_8), .C0(in_15), .Z0(in_14),
    .N0(in_13), .X(PCClkEN));
  Pull_Resistor pull_resistor_15 (.node(PCClkEN));
  PCOut pcout_1 (.A(in_1), .B(in_2), .X(PCout));
  Xin xin_1 (.A(in_1), .B(in_2), .C(in_3), .D(in_4), .E(in_5), .F(in_6), .G(in_7), .H(in_8), .X(Xin));
  Pull_Resistor pull_resistor_16 (.node(PCout));
  Pull_Resistor pull_resistor_17 (.node(Xin));
  Yin yin_1 (.A(in_1), .B(in_2), .C(in_3), .D(in_4), .E(in_5), .F(in_6), .G(in_7), .H(in_8), .X(Yin));
  Pull_Resistor pull_resistor_18 (.node(Yin));
  MSBin msbin_1 (.A(in_1), .B(in_2), .X(MSBin));
  Alt alt_1 (.A(in_1), .B(in_2), .C(in_3), .D(in_4), .E(in_5), .F(in_6), .G(in_7), .H(in_8), .X(out_34));
  Pull_Resistor pull_resistor_19 (.node(out_34));
  Pull_Resistor pull_resistor_20 (.node(MSBin));
  LSBin lsbin_1 (.A(in_1), .B(in_2), .X(LSBin));
  Pull_Resistor pull_resistor_21 (.node(LSBin));
  LSBout lsbout_1 (
    .A(in_1), .B(in_2), .C(in_3), .D(in_4), .E(in_5), .F(in_6), .G(in_7), .H(in_8), .C0(in_15), .Z0(in_14),
    .N0(in_13), .X(out_37));
  Pull_Resistor pull_resistor_22 (.node(out_37));
  Pull_Resistor pull_resistor_23 (.node(DO1));
  ALU_Control alu_control_1 (
    .A(in_1), .B(in_2), .C(in_3), .D(in_4), .E(in_5), .F(in_6), .G(in_7), .H(in_8), .X(DO1), .Y(out_39));
  Pull_Resistor pull_resistor_24 (.node(out_39));

  // Notes on the sheet:
  //   RAMEN
  //   ROM1out
  //   R1out
  //   R2out
  //   R4in
  //   PCLoad
  //   Alt
  //   LSBout
  //   DO0
endmodule

module MARin_C (
  input  A,
  input  B,
  input  C,
  input  D,
  input  E,
  input  F,
  input  G,
  input  H,
  output X
);

  wire and_1_out, and_2_out, not_1_out, not_2_out, not_3_out, not_4_out, not_5_out, or_1_out;

  not not_1 (not_1_out, A);
  not not_2 (not_2_out, B);
  not not_3 (not_3_out, C);
  not not_4 (not_4_out, E);
  not not_5 (not_5_out, F);
  and and_1 (and_1_out, not_1_out, not_2_out);
  and and_2 (and_2_out, A, B, not_3_out, D, not_4_out, not_5_out, G);
  or or_1 (or_1_out, and_1_out, and_2_out);
  assign X = or_1_out ? or_1_out : 1'bz;  // Controlled_Buffer controlled_buffer_1
endmodule

module RAMEN_C (
  input  A,
  input  B,
  input  C,
  input  D,
  input  E,
  input  F,
  input  G,
  input  H,
  output X
);

  wire not_1_out, not_2_out, not_3_out;

  not not_1 (not_1_out, D);
  not not_2 (not_2_out, E);
  not not_3 (not_3_out, F);
  and and_1 (X, A, B, C, not_1_out, not_2_out, not_3_out, G);
endmodule

module RAMData (
  input  A,
  input  B,
  input  C,
  input  D,
  input  E,
  input  F,
  input  G,
  input  H,
  output X
);

  wire not_1_out, not_2_out, not_3_out, not_4_out;

  not not_1 (not_1_out, D);
  not not_2 (not_2_out, E);
  not not_3 (not_3_out, F);
  not not_4 (not_4_out, H);
  and and_1 (X, A, B, C, not_1_out, not_2_out, not_3_out, G, not_4_out);
endmodule

module ROM1out (
  input  A,
  input  B,
  input  C,
  input  D,
  output X
);

  wire not_1_out, not_2_out, not_3_out;

  not not_1 (not_1_out, A);
  not not_2 (not_2_out, C);
  not not_3 (not_3_out, D);
  and and_1 (X, not_1_out, B, not_2_out, not_3_out);
endmodule

module Con_Clk_3 (
  input  SC,
  input  A,
  input  B,
  input  C,
  input  D,
  input  E,
  input  F,
  output X
);

  wire and_1_out, and_2_out, and_3_out, and_4_out, and_5_out, and_6_out, not_1_out, not_2_out, not_3_out,
       not_4_out, not_5_out;

  not not_1 (not_1_out, B);
  not not_2 (not_2_out, C);
  not not_3 (not_3_out, B);
  not not_4 (not_4_out, A);
  not not_5 (not_5_out, B);
  and and_1 (and_1_out, not_1_out, not_2_out, F);
  and and_2 (and_2_out, not_3_out, E);
  and and_3 (and_3_out, not_4_out, E, F);
  and and_4 (and_4_out, C, E, F);
  and and_5 (and_5_out, A, not_5_out, F);
  and and_6 (and_6_out, SC, E, F);
  or or_1 (X, and_1_out, and_2_out, and_3_out, and_4_out, and_5_out, and_6_out);
endmodule

module ROM2out (
  input  A,
  input  B,
  input  C,
  input  D,
  output X
);

  wire not_1_out, not_2_out, not_3_out;

  not not_1 (not_1_out, B);
  not not_2 (not_2_out, C);
  not not_3 (not_3_out, D);
  and and_1 (X, A, not_1_out, not_2_out, not_3_out);
endmodule

module PCLoad (
  input  A,
  input  B,
  input  C,
  input  D,
  input  E,
  input  F,
  input  G,
  input  H,
  input  C0,
  input  Z0,
  input  N0,
  output X
);

  wire and_1_out, and_2_out, and_3_out, and_4_out, not_1_out, not_2_out, not_3_out, not_4_out, not_5_out,
       not_6_out, not_7_out, not_8_out, not_9_out, not_10_out, not_11_out, not_12_out;

  not not_1 (not_1_out, C);
  not not_2 (not_2_out, F);
  not not_3 (not_3_out, G);
  not not_4 (not_4_out, H);
  not not_5 (not_5_out, C);
  not not_6 (not_6_out, F);
  not not_7 (not_7_out, H);
  not not_8 (not_8_out, C);
  not not_9 (not_9_out, F);
  not not_10 (not_10_out, G);
  not not_11 (not_11_out, C);
  not not_12 (not_12_out, F);
  and and_1 (and_1_out, A, B, not_1_out, D, E, not_2_out, not_3_out, not_4_out);
  and and_2 (and_2_out, A, B, not_5_out, D, E, not_6_out, not_7_out, Z0);
  and and_3 (and_3_out, A, B, not_8_out, D, E, not_9_out, not_10_out, C0);
  and and_4 (and_4_out, A, B, not_11_out, D, E, not_12_out, G, H, N0);
  or or_1 (X, and_1_out, and_2_out, and_3_out, and_4_out);
endmodule

module PCClkEN (
  input  A,
  input  B,
  input  C,
  input  D,
  input  E,
  input  F,
  input  G,
  input  H,
  input  C0,
  input  Z0,
  input  N0,
  output X
);

  wire and_1_out, and_2_out, and_3_out, and_4_out, and_5_out, not_1_out, not_2_out, not_3_out, not_4_out,
       not_5_out, not_6_out, not_7_out, not_8_out, not_9_out, not_10_out, not_11_out, not_12_out, not_13_out,
       not_14_out, not_15_out;

  not not_1 (not_1_out, C);
  not not_2 (not_2_out, F);
  not not_3 (not_3_out, G);
  not not_4 (not_4_out, H);
  not not_5 (not_5_out, C);
  not not_6 (not_6_out, F);
  not not_7 (not_7_out, H);
  not not_8 (not_8_out, C);
  not not_9 (not_9_out, F);
  not not_10 (not_10_out, G);
  not not_11 (not_11_out, C);
  not not_12 (not_12_out, F);
  not not_13 (not_13_out, A);
  not not_14 (not_14_out, C);
  not not_15 (not_15_out, D);
  and and_1 (and_1_out, A, B, not_1_out, D, E, not_2_out, not_3_out, not_4_out);
  and and_2 (and_2_out, A, B, not_5_out, D, E, not_6_out, not_7_out, Z0);
  and and_3 (and_3_out, A, B, not_8_out, D, E, not_9_out, not_10_out, C0);
  and and_4 (and_4_out, A, B, not_11_out, D, E, not_12_out, G, H, N0);
  and and_5 (and_5_out, not_13_out, B, not_14_out, not_15_out);
  or or_1 (X, and_1_out, and_2_out, and_3_out, and_4_out, and_5_out);
endmodule

module PCOut (
  input  A,
  input  B,
  output X
);

  wire not_1_out, not_2_out;

  not not_1 (not_1_out, A);
  not not_2 (not_2_out, B);
  and and_1 (X, not_1_out, not_2_out);
endmodule

module Xin (
  input  A,
  input  B,
  input  C,
  input  D,
  input  E,
  input  F,
  input  G,
  input  H,
  output X
);

  wire not_1_out;

  not not_1 (not_1_out, C);
  and and_1 (X, A, B, not_1_out, D, F);
endmodule

module Yin (
  input  A,
  input  B,
  input  C,
  input  D,
  input  E,
  input  F,
  input  G,
  input  H,
  output X
);

  wire not_1_out;

  not not_1 (not_1_out, D);
  and and_1 (X, A, B, C, not_1_out, F);
endmodule

module Alt (
  input  A,
  input  B,
  input  C,
  input  D,
  input  E,
  input  F,
  input  G,
  input  H,
  output X
);

  and and_1 (X, A, B, C, D, F, H);
endmodule

module MSBin (
  input  A,
  input  B,
  output X
);

  wire not_1_out;

  not not_1 (not_1_out, A);
  and and_1 (X, not_1_out, B);
endmodule

module LSBin (
  input  A,
  input  B,
  output X
);

  wire not_1_out;

  not not_1 (not_1_out, B);
  and and_1 (X, A, not_1_out);
endmodule

module LSBout (
  input  A,
  input  B,
  input  C,
  input  D,
  input  E,
  input  F,
  input  G,
  input  H,
  input  C0,
  input  Z0,
  input  N0,
  output X
);

  wire and_1_out, and_2_out, and_3_out, and_4_out, and_5_out, and_6_out, and_7_out, not_1_out, not_2_out,
       not_3_out, not_4_out, not_5_out, not_6_out, not_7_out, not_8_out, not_9_out, not_10_out, not_11_out,
       not_12_out, not_13_out, not_14_out, not_15_out, not_16_out, not_17_out, not_18_out, not_19_out;

  not not_1 (not_1_out, C);
  not not_2 (not_2_out, E);
  not not_3 (not_3_out, F);
  not not_4 (not_4_out, C);
  not not_5 (not_5_out, F);
  not not_6 (not_6_out, C);
  not not_7 (not_7_out, F);
  not not_8 (not_8_out, G);
  not not_9 (not_9_out, H);
  not not_10 (not_10_out, C);
  not not_11 (not_11_out, F);
  not not_12 (not_12_out, H);
  not not_13 (not_13_out, C);
  not not_14 (not_14_out, F);
  not not_15 (not_15_out, G);
  not not_16 (not_16_out, D);
  not not_17 (not_17_out, E);
  not not_18 (not_18_out, D);
  not not_19 (not_19_out, G);
  and and_1 (and_1_out, A, B, not_1_out, D, not_2_out, not_3_out, G);
  and and_2 (and_2_out, A, B, not_4_out, D, not_5_out, G, H, N0);
  and and_3 (and_3_out, A, B, not_6_out, D, E, not_7_out, not_8_out, not_9_out);
  and and_4 (and_4_out, A, B, not_10_out, D, E, not_11_out, not_12_out, Z0);
  and and_5 (and_5_out, A, B, not_13_out, D, E, not_14_out, not_15_out, C0);
  and and_6 (and_6_out, A, B, C, not_16_out, not_17_out, F, G, H);
  and and_7 (and_7_out, A, B, C, not_18_out, E, F, not_19_out);
  or or_1 (X, and_1_out, and_2_out, and_3_out, and_4_out, and_5_out, and_6_out, and_7_out);
endmodule

module ALU_Control (
  input  A,
  input  B,
  input  C,
  input  D,
  input  E,
  input  F,
  input  G,
  input  H,
  output X,
  output Y
);

  wire and_2_out, and_3_out, not_1_out, not_2_out;

  and and_1 (X, A, B, C, D, E, F);
  not not_1 (not_1_out, G);
  not not_2 (not_2_out, E);
  and and_2 (and_2_out, A, B, C, D, F, not_1_out);
  and and_3 (and_3_out, A, B, C, D, not_2_out, F, H);
  or or_1 (Y, and_2_out, and_3_out);
endmodule

module Reg_Control (
  input  A,
  input  B,
  input  C,
  input  D,
  input  E,
  input  F,
  input  G,
  input  H,
  input  P,
  input  Q,
  input  R,
  input  S,
  output R1in,
  output R1out,
  output R2in,
  output R2out,
  output R3in,
  output R3out,
  output R4in,
  output R4out
);

  wire and_2_out, and_3_out, and_4_out, and_5_out, and_6_out, and_7_out, and_9_out, and_10_out, and_11_out,
       and_12_out, and_13_out, and_14_out, and_16_out, and_17_out, and_18_out, and_19_out, and_20_out,
       and_21_out, and_22_out, and_23_out, and_24_out, and_25_out, and_26_out, and_27_out, and_28_out,
       and_29_out, and_30_out, and_31_out, and_32_out, and_33_out, not_1_out, not_2_out, not_3_out,
       not_4_out, not_5_out, not_6_out, not_7_out, not_8_out, not_9_out, not_10_out, not_11_out, not_12_out,
       not_13_out, not_14_out, not_15_out, not_16_out, not_17_out, not_18_out, not_19_out, not_20_out,
       not_21_out, not_22_out, not_23_out, not_24_out, not_25_out, not_26_out, not_27_out, not_28_out,
       not_29_out, not_30_out, not_31_out, not_32_out, not_33_out, not_34_out, not_35_out, not_36_out,
       not_37_out, not_38_out, not_39_out, not_40_out, not_41_out, not_42_out, not_43_out, not_44_out,
       not_45_out, not_46_out, not_47_out, not_48_out, not_49_out, not_50_out, not_51_out, not_52_out,
       not_53_out, not_54_out, not_55_out, not_56_out, not_57_out, not_58_out, not_59_out, not_60_out,
       not_61_out, not_62_out, not_63_out, not_64_out, not_65_out, not_66_out, not_67_out, not_68_out,
       not_69_out, not_70_out, not_71_out, not_72_out, not_73_out, not_74_out, not_75_out, not_76_out,
       not_77_out, not_78_out, not_79_out, not_80_out, not_81_out, not_82_out, not_83_out, not_84_out,
       not_85_out, not_86_out, not_87_out, not_88_out, not_89_out, not_90_out, not_91_out, not_92_out,
       not_93_out, not_94_out, not_95_out, not_96_out, not_97_out, not_98_out, not_99_out, not_100_out,
       not_101_out, not_102_out, not_103_out, not_104_out, not_105_out, not_106_out, not_107_out;

  not not_1 (not_1_out, C);
  not not_2 (not_2_out, E);
  not not_3 (not_3_out, F);
  not not_4 (not_4_out, G);
  not not_5 (not_5_out, R);
  not not_6 (not_6_out, S);
  not not_7 (not_7_out, C);
  not not_8 (not_8_out, E);
  not not_9 (not_9_out, G);
  not not_10 (not_10_out, P);
  not not_11 (not_11_out, Q);
  not not_12 (not_12_out, C);
  not not_13 (not_13_out, H);
  not not_14 (not_14_out, P);
  not not_15 (not_15_out, Q);
  not not_16 (not_16_out, C);
  not not_17 (not_17_out, P);
  not not_18 (not_18_out, Q);
  not not_19 (not_19_out, D);
  not not_20 (not_20_out, E);
  not not_21 (not_21_out, G);
  not not_22 (not_22_out, R);
  not not_23 (not_23_out, S);
  not not_24 (not_24_out, D);
  not not_25 (not_25_out, E);
  not not_26 (not_26_out, H);
  not not_27 (not_27_out, R);
  not not_28 (not_28_out, S);
  not not_29 (not_29_out, D);
  not not_30 (not_30_out, R);
  not not_31 (not_31_out, S);
  not not_32 (not_32_out, C);
  not not_33 (not_33_out, E);
  not not_34 (not_34_out, F);
  not not_35 (not_35_out, G);
  not not_36 (not_36_out, R);
  not not_37 (not_37_out, C);
  not not_38 (not_38_out, E);
  not not_39 (not_39_out, G);
  not not_40 (not_40_out, P);
  not not_41 (not_41_out, C);
  not not_42 (not_42_out, H);
  not not_43 (not_43_out, P);
  not not_44 (not_44_out, C);
  not not_45 (not_45_out, P);
  not not_46 (not_46_out, D);
  not not_47 (not_47_out, E);
  not not_48 (not_48_out, G);
  not not_49 (not_49_out, R);
  not not_50 (not_50_out, D);
  not not_51 (not_51_out, E);
  not not_52 (not_52_out, H);
  not not_53 (not_53_out, R);
  not not_54 (not_54_out, D);
  not not_55 (not_55_out, R);
  not not_56 (not_56_out, C);
  not not_57 (not_57_out, E);
  not not_58 (not_58_out, F);
  not not_59 (not_59_out, G);
  not not_60 (not_60_out, S);
  not not_61 (not_61_out, C);
  not not_62 (not_62_out, E);
  not not_63 (not_63_out, G);
  not not_64 (not_64_out, Q);
  not not_65 (not_65_out, C);
  not not_66 (not_66_out, H);
  not not_67 (not_67_out, Q);
  not not_68 (not_68_out, C);
  not not_69 (not_69_out, Q);
  not not_70 (not_70_out, D);
  not not_71 (not_71_out, E);
  not not_72 (not_72_out, G);
  not not_73 (not_73_out, S);
  not not_74 (not_74_out, D);
  not not_75 (not_75_out, E);
  not not_76 (not_76_out, H);
  not not_77 (not_77_out, S);
  not not_78 (not_78_out, D);
  not not_79 (not_79_out, S);
  not not_80 (not_80_out, C);
  not not_81 (not_81_out, E);
  not not_82 (not_82_out, F);
  not not_83 (not_83_out, G);
  not not_84 (not_84_out, D);
  not not_85 (not_85_out, E);
  not not_86 (not_86_out, F);
  not not_87 (not_87_out, H);
  not not_88 (not_88_out, E);
  not not_89 (not_89_out, G);
  not not_90 (not_90_out, C);
  not not_91 (not_91_out, E);
  not not_92 (not_92_out, G);
  not not_93 (not_93_out, C);
  not not_94 (not_94_out, H);
  not not_95 (not_95_out, C);
  not not_96 (not_96_out, D);
  not not_97 (not_97_out, E);
  not not_98 (not_98_out, F);
  not not_99 (not_99_out, D);
  not not_100 (not_100_out, E);
  not not_101 (not_101_out, G);
  not not_102 (not_102_out, D);
  not not_103 (not_103_out, E);
  not not_104 (not_104_out, H);
  not not_105 (not_105_out, D);
  not not_106 (not_106_out, C);
  not not_107 (not_107_out, E);
  and and_1 (R1in, A, B, not_1_out, D, not_2_out, not_3_out, not_4_out, H, not_5_out, not_6_out);
  and and_2 (and_2_out, A, B, not_7_out, D, not_8_out, not_9_out, H, not_10_out, not_11_out);
  and and_3 (and_3_out, A, B, not_12_out, D, F, not_13_out, not_14_out, not_15_out);
  and and_4 (and_4_out, A, B, not_16_out, D, E, F, not_17_out, not_18_out);
  and and_5 (and_5_out, A, B, C, not_19_out, not_20_out, F, not_21_out, not_22_out, not_23_out);
  and and_6 (and_6_out, A, B, C, not_24_out, not_25_out, F, not_26_out, not_27_out, not_28_out);
  and and_7 (and_7_out, A, B, C, not_29_out, E, F, G, not_30_out, not_31_out);
  and and_8 (R2in, A, B, not_32_out, D, not_33_out, not_34_out, not_35_out, H, not_36_out, S);
  and and_9 (and_9_out, A, B, not_37_out, D, not_38_out, not_39_out, H, not_40_out, Q);
  and and_10 (and_10_out, A, B, not_41_out, D, F, not_42_out, not_43_out, Q);
  and and_11 (and_11_out, A, B, not_44_out, D, E, F, not_45_out, Q);
  and and_12 (and_12_out, A, B, C, not_46_out, not_47_out, F, not_48_out, not_49_out, S);
  and and_13 (and_13_out, A, B, C, not_50_out, not_51_out, F, not_52_out, not_53_out, S);
  and and_14 (and_14_out, A, B, C, not_54_out, E, F, G, not_55_out, S);
  and and_15 (R3in, A, B, not_56_out, D, not_57_out, not_58_out, not_59_out, H, R, not_60_out);
  and and_16 (and_16_out, A, B, not_61_out, D, not_62_out, not_63_out, H, P, not_64_out);
  and and_17 (and_17_out, A, B, not_65_out, D, F, not_66_out, P, not_67_out);
  and and_18 (and_18_out, A, B, not_68_out, D, E, F, P, not_69_out);
  and and_19 (and_19_out, A, B, C, not_70_out, not_71_out, F, not_72_out, R, not_73_out);
  and and_20 (and_20_out, A, B, C, not_74_out, not_75_out, F, not_76_out, R, not_77_out);
  and and_21 (and_21_out, A, B, C, not_78_out, E, F, G, R, not_79_out);
  and and_22 (and_22_out, A, B, not_80_out, D, not_81_out, not_82_out, not_83_out, H, R, S);
  and and_23 (and_23_out, A, B, C, not_84_out, not_85_out, not_86_out, G, not_87_out);
  and and_24 (and_24_out, A, B, C, D, not_88_out, F, not_89_out);
  and and_25 (and_25_out, A, B, C, D, E, F, G);
  and and_26 (and_26_out, A, B, not_90_out, D, not_91_out, not_92_out, H, P, Q);
  and and_27 (and_27_out, A, B, not_93_out, D, F, not_94_out, P, Q);
  and and_28 (and_28_out, A, B, not_95_out, D, E, F, P, Q);
  and and_29 (and_29_out, A, B, C, not_96_out, not_97_out, not_98_out, G, H);
  and and_30 (and_30_out, A, B, C, not_99_out, not_100_out, F, not_101_out, R, S);
  and and_31 (and_31_out, A, B, C, not_102_out, not_103_out, F, not_104_out, R, S);
  and and_32 (and_32_out, A, B, C, not_105_out, E, F, G, R, S);
  and and_33 (and_33_out, A, B, not_106_out, D, not_107_out, F, G, H);
  or or_1 (R1out, and_2_out, and_3_out, and_4_out, and_5_out, and_6_out, and_7_out);
  or or_2 (R2out, and_9_out, and_10_out, and_11_out, and_12_out, and_13_out, and_14_out);
  or or_3 (R3out, and_16_out, and_17_out, and_18_out, and_19_out, and_20_out, and_21_out);
  or or_4 (R4in, and_22_out, and_23_out, and_24_out, and_25_out);
  or or_5 (R4out, and_26_out, and_27_out, and_28_out, and_29_out, and_30_out, and_31_out, and_32_out, and_33_out);
endmodule
