// Logisim project GPIO_Control.circ as structural Verilog: 1 circuit, main circuit GPIO_Control
module GPIO_Control (
  input  in_1,
  input  Reset,
  input  in_3,
  input  in_4,
  input  Clk,
  input  in_6,
  input  in_7,
  input  in_8,
  input  in_9,
  input  in_10,
  input  in_11,
  input  in_12,
  input  in_13,
  input  in_14,
  input  in_15,
  input  in_16,
  input  _7,
  input  _6,
  input  _5,
  input  _4,
  input  _3,
  input  _2,
  input  _1,
  input  _0,
  output out_25,
  output out_26,
  output out_27,
  output _7_2,
  output out_29,
  output _6_2,
  output _5_2,
  output _4_2,
  output _3_2,
  output _2_2,
  output _1_2,
  output _0_2
);

  wire general_purpose_register_1_out_9, general_purpose_register_1_out_10,
       general_purpose_register_1_out_11, general_purpose_register_1_out_12,
       general_purpose_register_1_out_13, general_purpose_register_1_out_14,
       general_purpose_register_1_out_15, general_purpose_register_1_out_16,
       general_purpose_register_2_out_9, general_purpose_register_2_out_10,
       general_purpose_register_2_out_11, general_purpose_register_2_out_12,
       general_purpose_register_2_out_13, general_purpose_register_2_out_14,
       general_purpose_register_2_out_15, general_purpose_register_2_out_16,
       general_purpose_register_3_out_9, general_purpose_register_3_out_10,
       general_purpose_register_3_out_11, general_purpose_register_3_out_12,
       general_purpose_register_3_out_13, general_purpose_register_3_out_14,
       general_purpose_register_3_out_15, general_purpose_register_3_out_16,
       general_purpose_register_4_out_9, general_purpose_register_4_out_10,
       general_purpose_register_4_out_11, general_purpose_register_4_out_12,
       general_purpose_register_4_out_13, general_purpose_register_4_out_14,
       general_purpose_register_4_out_15, general_purpose_register_4_out_16,
       general_purpose_register_5_out_9, general_purpose_register_5_out_10,
       general_purpose_register_5_out_11, general_purpose_register_5_out_12,
       general_purpose_register_6_out_9, general_purpose_register_6_out_10,
       general_purpose_register_6_out_11, general_purpose_register_6_out_12;

  assign out_25 = in_7 ? general_purpose_register_1_out_13 : 1'bz;  // Controlled_Buffer controlled_buffer_1
  assign out_26 = in_7 ? general_purpose_register_1_out_14 : 1'bz;  // Controlled_Buffer controlled_buffer_2
  assign out_27 = in_7 ? general_purpose_register_1_out_15 : 1'bz;  // Controlled_Buffer controlled_buffer_3
  assign out_29 = in_7 ? general_purpose_register_1_out_16 : 1'bz;  // Controlled_Buffer controlled_buffer_4
  assign out_25 = in_8 ? general_purpose_register_2_out_13 : 1'bz;  // Controlled_Buffer controlled_buffer_5
  assign out_26 = in_8 ? general_purpose_register_2_out_14 : 1'bz;  // Controlled_Buffer controlled_buffer_6
  assign out_27 = in_8 ? general_purpose_register_2_out_15 : 1'bz;  // Controlled_Buffer controlled_buffer_7
  assign out_29 = in_8 ? general_purpose_register_2_out_16 : 1'bz;  // Controlled_Buffer controlled_buffer_8
  assign out_25 = in_9 ? general_purpose_register_3_out_13 : 1'bz;  // Controlled_Buffer controlled_buffer_9
  assign out_26 = in_9 ? general_purpose_register_3_out_14 : 1'bz;  // Controlled_Buffer controlled_buffer_10
  assign out_27 = in_9 ? general_purpose_register_3_out_15 : 1'bz;  // Controlled_Buffer controlled_buffer_11
  assign out_29 = in_9 ? general_purpose_register_3_out_16 : 1'bz;  // Controlled_Buffer controlled_buffer_12
  assign out_25 = in_10 ? general_purpose_register_4_out_13 : 1'bz;  // Controlled_Buffer controlled_buffer_13
  assign out_26 = in_10 ? general_purpose_register_4_out_14 : 1'bz;  // Controlled_Buffer controlled_buffer_14
  assign out_27 = in_10 ? general_purpose_register_4_out_15 : 1'bz;  // Controlled_Buffer controlled_buffer_15
  assign out_29 = in_10 ? general_purpose_register_4_out_16 : 1'bz;  // Controlled_Buffer controlled_buffer_16
  General_Purpose_Register general_purpose_register_1 (
    .in_5(in_13), .in_6(Clk), .in_8(1'b1), .in_1(in_1), .in_2(in_3), .in_3(in_4), .in_4(in_6),
    .out_13(general_purpose_register_1_out_13), .out_14(general_purpose_register_1_out_14),
    .out_15(general_purpose_register_1_out_15), .out_16(general_purpose_register_1_out_16),
    .out_9(general_purpose_register_1_out_9), .out_10(general_purpose_register_1_out_10),
    .out_11(general_purpose_register_1_out_11), .out_12(general_purpose_register_1_out_12), .in_7(Reset));
  LED led_1 (.in(general_purpose_register_1_out_9));
  General_Purpose_Register general_purpose_register_2 (
    .in_5(in_14), .in_6(Clk), .in_8(1'b1), .in_1(in_1), .in_2(in_3), .in_3(in_4), .in_4(in_6),
    .out_13(general_purpose_register_2_out_13), .out_14(general_purpose_register_2_out_14),
    .out_15(general_purpose_register_2_out_15), .out_16(general_purpose_register_2_out_16),
    .out_9(general_purpose_register_2_out_9), .out_10(general_purpose_register_2_out_10),
    .out_11(general_purpose_register_2_out_11), .out_12(general_purpose_register_2_out_12), .in_7(Reset));
  LED led_2 (.in(general_purpose_register_2_out_9));
  General_Purpose_Register general_purpose_register_3 (
    .in_5(in_15), .in_6(Clk), .in_8(1'b1), .in_1(in_1), .in_2(in_3), .in_3(in_4), .in_4(in_6),
    .out_13(general_purpose_register_3_out_13), .out_14(general_purpose_register_3_out_14),
    .out_15(general_purpose_register_3_out_15), .out_16(general_purpose_register_3_out_16),
    .out_9(general_purpose_register_3_out_9), .out_10(general_purpose_register_3_out_10),
    .out_11(general_purpose_register_3_out_11), .out_12(general_purpose_register_3_out_12), .in_7(Reset));
  LED led_3 (.in(general_purpose_register_3_out_9));
  General_Purpose_Register general_purpose_register_4 (
    .in_5(in_16), .in_6(Clk), .in_8(1'b1), .in_1(in_1), .in_2(in_3), .in_3(in_4), .in_4(in_6),
    .out_13(general_purpose_register_4_out_13), .out_14(general_purpose_register_4_out_14),
    .out_15(general_purpose_register_4_out_15), .out_16(general_purpose_register_4_out_16),
    .out_9(general_purpose_register_4_out_9), .out_10(general_purpose_register_4_out_10),
    .out_11(general_purpose_register_4_out_11), .out_12(general_purpose_register_4_out_12), .in_7(Reset));
  LED led_4 (.in(general_purpose_register_4_out_9));
  General_Purpose_Register general_purpose_register_5 (
    .in_5(1'b1), .in_6(Clk), .in_8(in_11), .in_1(_3), .in_2(_2), .in_3(_1), .in_4(_0), .out_13(out_25),
    .out_14(out_26), .out_15(out_27), .out_16(out_29), .out_9(general_purpose_register_5_out_9),
    .out_10(general_purpose_register_5_out_10), .out_11(general_purpose_register_5_out_11),
    .out_12(general_purpose_register_5_out_12), .in_7(Reset));
  LED led_5 (.in(general_purpose_register_5_out_9));
  General_Purpose_Register general_purpose_register_6 (
    .in_5(1'b1), .in_6(Clk), .in_8(in_12), .in_1(_7), .in_2(_6), .in_3(_5), .in_4(_4), .out_13(out_25),
    .out_14(out_26), .out_15(out_27), .out_16(out_29), .out_9(general_purpose_register_6_out_9),
    .out_10(general_purpose_register_6_out_10), .out_11(general_purpose_register_6_out_11),
    .out_12(general_purpose_register_6_out_12), .in_7(Reset));
  LED led_6 (.in(general_purpose_register_6_out_9));
  LED led_7 (.in(general_purpose_register_1_out_10));
  LED led_8 (.in(general_purpose_register_1_out_12));
  LED led_9 (.in(general_purpose_register_1_out_11));
  LED led_10 (.in(general_purpose_register_2_out_12));
  LED led_11 (.in(general_purpose_register_2_out_11));
  LED led_12 (.in(general_purpose_register_2_out_10));
  LED led_13 (.in(general_purpose_register_3_out_12));
  LED led_14 (.in(general_purpose_register_3_out_10));
  LED led_15 (.in(general_purpose_register_3_out_11));
  LED led_16 (.in(general_purpose_register_4_out_12));
  LED led_17 (.in(general_purpose_register_4_out_10));
  LED led_18 (.in(general_purpose_register_4_out_11));
  LED led_19 (.in(general_purpose_register_5_out_12));
  LED led_20 (.in(general_purpose_register_5_out_10));
  LED led_21 (.in(general_purpose_register_5_out_11));
  LED led_22 (.in(general_purpose_register_6_out_10));
  LED led_23 (.in(general_purpose_register_6_out_11));
  LED led_24 (.in(general_purpose_register_6_out_12));
  assign _7_2 = general_purpose_register_2_out_13 ? general_purpose_register_4_out_13 : 1'bz;  // Controlled_Buffer controlled_buffer_17
  assign _6_2 = general_purpose_register_2_out_14 ? general_purpose_register_4_out_14 : 1'bz;  // Controlled_Buffer controlled_buffer_18
  assign _5_2 = general_purpose_register_2_out_15 ? general_purpose_register_4_out_15 : 1'bz;  // Controlled_Buffer controlled_buffer_19
  assign _4_2 = general_purpose_register_2_out_16 ? general_purpose_register_4_out_16 : 1'bz;  // Controlled_Buffer controlled_buffer_20
  assign _3_2 = general_purpose_register_1_out_13 ? general_purpose_register_3_out_13 : 1'bz;  // Controlled_Buffer controlled_buffer_21
  assign _2_2 = general_purpose_register_1_out_14 ? general_purpose_register_3_out_14 : 1'bz;  // Controlled_Buffer controlled_buffer_22
  assign _1_2 = general_purpose_register_1_out_15 ? general_purpose_register_3_out_15 : 1'bz;  // Controlled_Buffer controlled_buffer_23
  assign _0_2 = general_purpose_register_1_out_16 ? general_purpose_register_3_out_16 : 1'bz;  // Controlled_Buffer controlled_buffer_24

  // Notes on the sheet:
  //   Data Direction
  //   Data Direction
  //   OUT Pins
  //   OUT Pins
  //   IN Pins
  //   IN Pins
endmodule
