// Logisim project Instruction Register.circ as structural Verilog: 1 circuit, main circuit Instruction Register
module Instruction_Register (
  input  in_1,
  input  in_2,
  input  in_3,
  input  in_4,
  input  in_5,
  input  in_6,
  input  in_7,
  input  in_8,
  input  in_9,
  output out_10,
  output out_11,
  output out_12,
  output out_13,
  output out_14,
  output out_15,
  output out_16,
  output out_17,
  output out_18,
  output out_19,
  output out_20,
  output out_21
);

  General_Purpose_Register general_purpose_register_1 (
    .in_5(in_6), .in_6(in_8), .in_8(1'b1), .in_1(in_1), .in_2(in_2), .in_3(in_3), .in_4(in_4),
    .out_13(out_14), .out_14(out_15), .out_15(out_16), .out_16(out_17), .in_7(in_5));  // open: out_9, out_10, out_11, out_12
  General_Purpose_Register general_purpose_register_2 (
    .in_5(in_7), .in_6(in_8), .in_8(1'b1), .in_1(in_1), .in_2(in_2), .in_3(in_3), .in_4(in_4),
    .out_13(out_18), .out_14(out_19), .out_15(out_20), .out_16(out_21), .in_7(in_5));  // open: out_9, out_10, out_11, out_12
  assign out_10 = in_9 ? out_18 : 1'bz;  // Controlled_Buffer controlled_buffer_1
  assign out_11 = in_9 ? out_19 : 1'bz;  // Controlled_Buffer controlled_buffer_2
  assign out_12 = in_9 ? out_20 : 1'bz;  // Controlled_Buffer controlled_buffer_3
  assign out_13 = in_9 ? out_21 : 1'bz;  // Controlled_Buffer controlled_buffer_4
endmodule
