// Logisim project Memory Management.circ as structural Verilog: 2 circuits, main circuit Memory Management with RAM
module Memory_Management_with_RAM (
  input  in_1,
  input  in_2,
  input  in_3,
  input  in_4,
  input  in_5,
  input  in_6,
  input  in_7,
  input  in_8,
  input  in_9,
  output out_10,
  output out_11,
  output out_12,
  output out_13,
  output out_14,
  output out_15,
  output out_16,
  output out_17,
  output out_18,
  output out_19,
  output out_20,
  output out_21,
  output out_22,
  output out_23
);

  wire general_purpose_register_1_out_9, general_purpose_register_1_out_10,
       general_purpose_register_1_out_11, general_purpose_register_1_out_12, memory_management_1_ram_en_out,
       not_1_out;
  wire [3:0] general_purpose_register_1_out_16, ram_1_data;

  General_Purpose_Register general_purpose_register_1 (
    .in_5(in_7), .in_6(in_8), .in_8(1'b1), .in_1(in_2), .in_2(in_3), .in_3(in_4), .in_4(in_5),
    .out_13(general_purpose_register_1_out_16[3]), .out_14(general_purpose_register_1_out_16[2]),
    .out_15(general_purpose_register_1_out_16[1]), .out_16(general_purpose_register_1_out_16[0]),
    .out_9(general_purpose_register_1_out_9), .out_10(general_purpose_register_1_out_10),
    .out_11(general_purpose_register_1_out_11), .out_12(general_purpose_register_1_out_12), .in_7(in_6));
  LED led_1 (.in(general_purpose_register_1_out_9));
  LED led_2 (.in(general_purpose_register_1_out_11));
  LED led_3 (.in(general_purpose_register_1_out_10));
  LED led_4 (.in(general_purpose_register_1_out_12));
  Memory_Management memory_management_1 (
    .A3(general_purpose_register_1_out_16[3]), .A2(general_purpose_register_1_out_16[2]),
    .A1(general_purpose_register_1_out_16[1]), .A0(general_purpose_register_1_out_16[0]), .RAM_EN(in_1),
    .DATA_OUT(in_9), .R1in(out_16), .R1out(out_10), .R2in(out_17), .R2out(out_11), .R3in(out_18),
    .R3out(out_12), .R4in(out_19), .R4out(out_13), .R5out(out_14), .R6out(out_15),
    .RAM_EN_OUT(memory_management_1_ram_en_out));
  RAM #(.addrWidth(4), .dataWidth(4)) ram_1 (
    .addr(general_purpose_register_1_out_16), .data(ram_1_data), .sel(memory_management_1_ram_en_out),
    .clk(in_8), .ld(in_9), .clr(1'b0));
  assign ram_1_data = not_1_out ? {in_2, in_3, in_4, in_5} : 4'bz;  // Controlled_Buffer controlled_buffer_1
  not not_1 (not_1_out, in_9);
  assign {out_20, out_21, out_22, out_23} = in_9 ? ram_1_data : 4'bz;  // Controlled_Buffer controlled_buffer_2

  // Notes on the sheet:
  //   RAM
endmodule

module Memory_Management (
  input  A3,
  input  A2,
  input  A1,
  input  A0,
  input  RAM_EN,
  input  DATA_OUT,
  output R1in,
  output R1out,
  output R2in,
  output R2out,
  output RAM_EN_OUT,
  output R3in,
  output R3out,
  output R4in,
  output R4out,
  output R5out,
  output R6out
);

  wire nor_1_out, not_1_out, not_2_out, not_3_out, not_4_out, not_5_out, not_6_out, not_7_out, not_8_out,
       not_9_out, not_10_out, not_11_out, not_12_out, not_13_out, not_14_out, not_15_out, not_16_out,
       not_17_out;

  not not_1 (not_1_out, A2);
  not not_2 (not_2_out, A0);
  not not_3 (not_3_out, DATA_OUT);
  not not_4 (not_4_out, A2);
  not not_5 (not_5_out, A0);
  not not_6 (not_6_out, A2);
  not not_7 (not_7_out, DATA_OUT);
  not not_8 (not_8_out, A2);
  not not_9 (not_9_out, A1);
  not not_10 (not_10_out, A0);
  not not_11 (not_11_out, DATA_OUT);
  not not_12 (not_12_out, A1);
  not not_13 (not_13_out, A0);
  not not_14 (not_14_out, A1);
  not not_15 (not_15_out, DATA_OUT);
  not not_16 (not_16_out, A1);
  not not_17 (not_17_out, A0);
  and and_1 (R6out, A3, A2, A1, A0, RAM_EN, DATA_OUT);
  and and_2 (R1in, A3, not_1_out, A1, not_2_out, RAM_EN, not_3_out);
  and and_3 (R1out, A3, not_4_out, A1, not_5_out, RAM_EN, DATA_OUT);
  and and_4 (R2in, A3, not_6_out, A1, A0, RAM_EN, not_7_out);
  and and_5 (R2out, A3, not_8_out, A1, A0, RAM_EN, DATA_OUT);
  and and_6 (R3in, A3, A2, not_9_out, not_10_out, RAM_EN, not_11_out);
  and and_7 (R3out, A3, A2, not_12_out, not_13_out, RAM_EN, DATA_OUT);
  and and_8 (R4in, A3, A2, not_14_out, A0, RAM_EN, not_15_out);
  and and_9 (R4out, A3, A2, not_16_out, A0, RAM_EN, DATA_OUT);
  and and_10 (R5out, A3, A2, A1, not_17_out, RAM_EN, DATA_OUT);
  nor nor_1 (nor_1_out, R1in, R1out, R2in, R2out, R3in, R3out, R4in, R4out, R5out, R6out);
  and and_11 (RAM_EN_OUT, nor_1_out, RAM_EN);
endmodule
