// Logisim project GPIO_test.circ as structural Verilog: 1 circuit, main circuit main
module main (
  input  in_1,
  output out_2
);

  wire button_1_out, clock_1_out;

  Button button_1 (.out(button_1_out));
  Clock clock_1 (.out(clock_1_out));
  Architecture1 architecture1_1 (
    .Reset(button_1_out), .in_3(out_2), .in_10(in_1), .out_11(out_2), .out_18(in_1), .Clk(clock_1_out));  // open: in_4, in_5, in_6, in_7, in_8, in_9, out_12, out_13, out_14, out_15, out_16, out_17
endmodule
