// Logisim project Up, Down Counter Program.circ as structural Verilog: 1 circuit, main circuit main
module main (
  input  in_1
);

  wire button_1_out, clock_1_out;
  wire [3:0] architecture1_1_out_14;

  Button button_1 (.out(button_1_out));
  Clock clock_1 (.out(clock_1_out));
  Architecture1 architecture1_1 (
    .Reset(button_1_out), .in_3(architecture1_1_out_14[3]), .in_4(architecture1_1_out_14[2]),
    .in_5(architecture1_1_out_14[1]), .in_6(architecture1_1_out_14[0]), .in_10(in_1),
    .out_11(architecture1_1_out_14[3]), .out_12(architecture1_1_out_14[2]),
    .out_13(architecture1_1_out_14[1]), .out_14(architecture1_1_out_14[0]), .out_18(in_1), .Clk(clock_1_out));  // open: in_7, in_8, in_9, out_15, out_16, out_17
  Hex_Digit_Display hex_digit_display_1 (.value(architecture1_1_out_14));  // open: dp
endmodule
