// Logisim project Microcontroller_Architecture.circ as structural Verilog: 1 circuit, main circuit Architecture1
module Architecture1 (
  input  Clk,
  input  Reset,
  input  in_3,
  input  in_4,
  input  in_5,
  input  in_6,
  input  in_7,
  input  in_8,
  input  in_9,
  input  in_10,
  output out_11,
  output out_12,
  output out_13,
  output out_14,
  output out_15,
  output out_16,
  output out_17,
  output out_18
);

  wire architecture1_1_a0_out, architecture1_1_a1_out, architecture1_1_a2_out, architecture1_1_a3_out,
       architecture1_1_data_in_bar___data_out, architecture1_1_marin, architecture1_1_ram_en,
       architecture1_1_rom1_out, architecture1_1_rom2_out, memory_management_with_ram_1_out_10,
       memory_management_with_ram_1_out_11, memory_management_with_ram_1_out_12,
       memory_management_with_ram_1_out_13, memory_management_with_ram_1_out_14,
       memory_management_with_ram_1_out_15, memory_management_with_ram_1_out_16,
       memory_management_with_ram_1_out_17, memory_management_with_ram_1_out_18,
       memory_management_with_ram_1_out_19;

  CPU_Architecture_Architecture1 architecture1_1 (
    .MARin(architecture1_1_marin), .RAM_EN(architecture1_1_ram_en),
    .Data_in_bar___Data_out(architecture1_1_data_in_bar___data_out), .ROM1_out(architecture1_1_rom1_out),
    .ROM2_out(architecture1_1_rom2_out), .A3_out(architecture1_1_a3_out), .A2_out(architecture1_1_a2_out),
    .A1_out(architecture1_1_a1_out), .A0_out(architecture1_1_a0_out), .Clk(Clk),
    .A3_in(architecture1_1_a3_out), .A2_in(architecture1_1_a2_out), .A1_in(architecture1_1_a1_out),
    .A0_in(architecture1_1_a0_out), .in_1(Reset));
  ROM_with_MAR rom_with_mar_1 (
    .in_1(architecture1_1_a0_out), .in_2(architecture1_1_a1_out), .in_3(architecture1_1_a2_out),
    .in_4(architecture1_1_a3_out), .in_6(architecture1_1_marin), .in_7(Clk), .in_8(architecture1_1_rom1_out),
    .in_9(architecture1_1_rom2_out), .in_5(Reset), .out_10(architecture1_1_a0_out),
    .out_11(architecture1_1_a1_out), .out_12(architecture1_1_a2_out), .out_13(architecture1_1_a3_out));
  LED led_1 (.in(architecture1_1_a3_out));
  Pull_Resistor pull_resistor_1 (.node(architecture1_1_a3_out));
  LED led_2 (.in(architecture1_1_a2_out));
  LED led_3 (.in(architecture1_1_a0_out));
  LED led_4 (.in(architecture1_1_a1_out));
  Pull_Resistor pull_resistor_2 (.node(architecture1_1_a2_out));
  Pull_Resistor pull_resistor_3 (.node(architecture1_1_a0_out));
  Pull_Resistor pull_resistor_4 (.node(architecture1_1_a1_out));
  Memory_Management_with_RAM memory_management_with_ram_1 (
    .in_1(architecture1_1_ram_en), .in_2(architecture1_1_a3_out), .in_3(architecture1_1_a2_out),
    .in_4(architecture1_1_a1_out), .in_5(architecture1_1_a0_out), .in_6(Reset), .in_7(architecture1_1_marin),
    .in_8(Clk), .in_9(architecture1_1_data_in_bar___data_out), .out_20(architecture1_1_a3_out),
    .out_21(architecture1_1_a2_out), .out_22(architecture1_1_a1_out), .out_23(architecture1_1_a0_out),
    .out_10(memory_management_with_ram_1_out_10), .out_11(memory_management_with_ram_1_out_11),
    .out_12(memory_management_with_ram_1_out_12), .out_13(memory_management_with_ram_1_out_13),
    .out_14(memory_management_with_ram_1_out_14), .out_15(memory_management_with_ram_1_out_15),
    .out_16(memory_management_with_ram_1_out_16), .out_17(memory_management_with_ram_1_out_17),
    .out_18(memory_management_with_ram_1_out_18), .out_19(memory_management_with_ram_1_out_19));
  GPIO_Control gpio_control_1 (
    .Reset(Reset), ._7_2(out_11), ._6_2(out_12), ._5_2(out_13), ._4_2(out_14), ._3_2(out_15), ._2_2(out_16),
    ._1_2(out_17), ._0_2(out_18), ._7(in_3), ._6(in_4), ._5(in_5), ._4(in_6), ._3(in_7), ._2(in_8),
    ._1(in_9), ._0(in_10), .in_1(architecture1_1_a3_out), .in_3(architecture1_1_a2_out),
    .in_4(architecture1_1_a1_out), .in_6(architecture1_1_a0_out), .out_25(architecture1_1_a3_out),
    .out_26(architecture1_1_a2_out), .out_27(architecture1_1_a1_out), .out_29(architecture1_1_a0_out),
    .in_7(memory_management_with_ram_1_out_10), .in_8(memory_management_with_ram_1_out_11),
    .in_9(memory_management_with_ram_1_out_12), .in_10(memory_management_with_ram_1_out_13),
    .in_11(memory_management_with_ram_1_out_14), .in_12(memory_management_with_ram_1_out_15),
    .in_13(memory_management_with_ram_1_out_16), .in_14(memory_management_with_ram_1_out_17),
    .in_15(memory_management_with_ram_1_out_18), .in_16(memory_management_with_ram_1_out_19), .Clk(Clk));
endmodule
