// Logisim project Nand_Xor_control_logic.circ as structural Verilog: 1 circuit, main circuit NandXorControlLogic
module NandXorControlLogic (
  input  in_1,
  input  in_2,
  input  in_3,
  input  in_4,
  input  in_5,
  input  in_6,
  input  in_7,
  input  in_8,
  input  in_9,
  output out_10,
  output out_11,
  output out_12,
  output out_13
);

  wire nand_1_out, nand_2_out, nand_3_out, nand_4_out, not_1_out, xor_1_out, xor_2_out, xor_3_out, xor_4_out;

  not not_1 (not_1_out, in_9);
  nand nand_1 (nand_1_out, in_1, in_5);
  assign out_10 = not_1_out ? nand_1_out : 1'bz;  // Controlled_Buffer controlled_buffer_1
  nand nand_2 (nand_2_out, in_2, in_6);
  assign out_11 = not_1_out ? nand_2_out : 1'bz;  // Controlled_Buffer controlled_buffer_2
  nand nand_3 (nand_3_out, in_3, in_7);
  assign out_12 = not_1_out ? nand_3_out : 1'bz;  // Controlled_Buffer controlled_buffer_3
  nand nand_4 (nand_4_out, in_4, in_8);
  assign out_13 = not_1_out ? nand_4_out : 1'bz;  // Controlled_Buffer controlled_buffer_4
  xor xor_1 (xor_1_out, in_1, in_5);
  assign out_10 = in_9 ? xor_1_out : 1'bz;  // Controlled_Buffer controlled_buffer_5
  xor xor_2 (xor_2_out, in_2, in_6);
  assign out_11 = in_9 ? xor_2_out : 1'bz;  // Controlled_Buffer controlled_buffer_6
  xor xor_3 (xor_3_out, in_3, in_7);
  assign out_12 = in_9 ? xor_3_out : 1'bz;  // Controlled_Buffer controlled_buffer_7
  xor xor_4 (xor_4_out, in_4, in_8);
  assign out_13 = in_9 ? xor_4_out : 1'bz;  // Controlled_Buffer controlled_buffer_8
endmodule
