// Logisim project Program Counter.circ as structural Verilog: 1 circuit, main circuit Program counter
module Program_counter (
  input  in_1,
  input  in_2,
  input  in_3,
  input  in_4,
  input  in_5,
  input  in_6,
  input  in_7,
  input  in_8,
  input  in_9,
  output out_10,
  output out_11,
  output out_12,
  output out_13,
  output out_14,
  output out_15,
  output out_16,
  output out_17
);

  wire controlled_buffer_1_out, controlled_buffer_2_out, controlled_buffer_4_out, controlled_buffer_6_out,
       controlled_buffer_8_out, controlled_buffer_10_out, controlled_buffer_12_out, controlled_buffer_14_out,
       controlled_buffer_16_out, controlled_buffer_18_out, controlled_buffer_20_out,
       controlled_buffer_22_out, d_ff_1_qn, d_ff_2_qn, d_ff_3_qn, d_ff_4_qn, not_1_out, not_2_out, not_3_out,
       not_4_out, not_5_out;

  assign controlled_buffer_1_out = in_7 ? in_6 : 1'bz;  // Controlled_Buffer controlled_buffer_1
  not not_1 (not_1_out, in_5);
  assign controlled_buffer_2_out = in_5 ? controlled_buffer_1_out : 1'bz;  // Controlled_Buffer controlled_buffer_2
  assign controlled_buffer_2_out = not_1_out ? d_ff_2_qn : 1'bz;  // Controlled_Buffer controlled_buffer_3
  assign controlled_buffer_4_out = not_2_out ? d_ff_1_qn : 1'bz;  // Controlled_Buffer controlled_buffer_4
  not not_2 (not_2_out, in_5);
  assign controlled_buffer_4_out = in_5 ? controlled_buffer_6_out : 1'bz;  // Controlled_Buffer controlled_buffer_5
  assign controlled_buffer_6_out = in_5 ? in_1 : 1'bz;  // Controlled_Buffer controlled_buffer_6
  D_Flip_Flop d_ff_1 (
    .clk(controlled_buffer_2_out), .D(controlled_buffer_4_out), .Q(out_10), .Qn(d_ff_1_qn), .reset(in_8));  // open: preset, en
  assign out_14 = in_9 ? out_10 : 1'bz;  // Controlled_Buffer controlled_buffer_7
  assign controlled_buffer_8_out = in_5 ? controlled_buffer_1_out : 1'bz;  // Controlled_Buffer controlled_buffer_8
  assign controlled_buffer_8_out = not_1_out ? d_ff_3_qn : 1'bz;  // Controlled_Buffer controlled_buffer_9
  D_Flip_Flop d_ff_2 (
    .clk(controlled_buffer_8_out), .D(controlled_buffer_10_out), .Q(out_11), .Qn(d_ff_2_qn), .reset(in_8));  // open: preset, en
  assign controlled_buffer_10_out = not_3_out ? d_ff_2_qn : 1'bz;  // Controlled_Buffer controlled_buffer_10
  not not_3 (not_3_out, in_5);
  assign controlled_buffer_10_out = in_5 ? controlled_buffer_12_out : 1'bz;  // Controlled_Buffer controlled_buffer_11
  assign controlled_buffer_12_out = in_5 ? in_2 : 1'bz;  // Controlled_Buffer controlled_buffer_12
  assign out_15 = in_9 ? out_11 : 1'bz;  // Controlled_Buffer controlled_buffer_13
  assign controlled_buffer_14_out = in_5 ? controlled_buffer_1_out : 1'bz;  // Controlled_Buffer controlled_buffer_14
  assign controlled_buffer_14_out = not_1_out ? d_ff_4_qn : 1'bz;  // Controlled_Buffer controlled_buffer_15
  D_Flip_Flop d_ff_3 (
    .clk(controlled_buffer_14_out), .D(controlled_buffer_16_out), .Q(out_12), .Qn(d_ff_3_qn), .reset(in_8));  // open: preset, en
  assign controlled_buffer_16_out = not_4_out ? d_ff_3_qn : 1'bz;  // Controlled_Buffer controlled_buffer_16
  not not_4 (not_4_out, in_5);
  assign controlled_buffer_16_out = in_5 ? controlled_buffer_18_out : 1'bz;  // Controlled_Buffer controlled_buffer_17
  assign controlled_buffer_18_out = in_5 ? in_3 : 1'bz;  // Controlled_Buffer controlled_buffer_18
  assign out_16 = in_9 ? out_12 : 1'bz;  // Controlled_Buffer controlled_buffer_19
  D_Flip_Flop d_ff_4 (
    .clk(controlled_buffer_1_out), .D(controlled_buffer_20_out), .Q(out_13), .Qn(d_ff_4_qn), .reset(in_8));  // open: preset, en
  assign controlled_buffer_20_out = not_5_out ? d_ff_4_qn : 1'bz;  // Controlled_Buffer controlled_buffer_20
  not not_5 (not_5_out, in_5);
  assign controlled_buffer_20_out = in_5 ? controlled_buffer_22_out : 1'bz;  // Controlled_Buffer controlled_buffer_21
  assign controlled_buffer_22_out = in_5 ? in_4 : 1'bz;  // Controlled_Buffer controlled_buffer_22
  assign out_17 = in_9 ? out_13 : 1'bz;  // Controlled_Buffer controlled_buffer_23
endmodule
