// Logisim project ROM with MAR.circ as structural Verilog: 1 circuit, main circuit ROM with MAR
module ROM_with_MAR (
  input  in_1,
  input  in_2,
  input  in_3,
  input  in_4,
  input  in_5,
  input  in_6,
  input  in_7,
  input  in_8,
  input  in_9,
  output out_10,
  output out_11,
  output out_12,
  output out_13
);

  wire general_purpose_register_1_out_9, general_purpose_register_1_out_10,
       general_purpose_register_1_out_11, general_purpose_register_1_out_12;
  wire [3:0] general_purpose_register_1_out_16, rom_1_data, rom_2_data;

  General_Purpose_Register general_purpose_register_1 (
    .in_5(in_6), .in_6(in_7), .in_8(1'b1), .in_1(in_4), .in_2(in_3), .in_3(in_2), .in_4(in_1),
    .out_13(general_purpose_register_1_out_16[3]), .out_14(general_purpose_register_1_out_16[2]),
    .out_15(general_purpose_register_1_out_16[1]), .out_16(general_purpose_register_1_out_16[0]),
    .out_9(general_purpose_register_1_out_9), .out_10(general_purpose_register_1_out_10),
    .out_11(general_purpose_register_1_out_11), .out_12(general_purpose_register_1_out_12), .in_7(in_5));
  LED led_1 (.in(general_purpose_register_1_out_9));
  LED led_2 (.in(general_purpose_register_1_out_10));
  LED led_3 (.in(general_purpose_register_1_out_11));
  LED led_4 (.in(general_purpose_register_1_out_12));
  ROM #(.addrWidth(4), .dataWidth(4)) rom_1 (.addr(general_purpose_register_1_out_16), .data(rom_1_data), .sel(in_8));
  assign {out_13, out_12, out_11, out_10} = in_8 ? rom_1_data : 4'bz;  // Controlled_Buffer controlled_buffer_1
  assign {out_13, out_12, out_11, out_10} = in_9 ? rom_2_data : 4'bz;  // Controlled_Buffer controlled_buffer_2
  ROM #(.addrWidth(4), .dataWidth(4)) rom_2 (.addr(general_purpose_register_1_out_16), .data(rom_2_data), .sel(in_9));

  // Notes on the sheet:
  //   ROM 1
  //   contents of rom_1 (hex, n*v repeats v):
  //   f 0 f
  //   ROM 2
  //   contents of rom_2 (hex, n*v repeats v):
  //   f 0 f
endmodule
