// Logisim project Shift - Rotate Register.circ as structural Verilog: 1 circuit, main circuit Shift-Rotate Register
module Shift_Rotate_Register (
  input  in_1,
  input  in_2,
  input  in_3,
  input  in_4,
  input  in_5,
  input  in_6,
  input  in_7,
  output out_8,
  output out_9,
  output out_10,
  output out_11,
  output out_12
);

  wire and_1_out, controlled_buffer_1_out, controlled_buffer_2_out, controlled_buffer_3_out,
       controlled_buffer_4_out, controlled_buffer_5_out, controlled_buffer_6_out, controlled_buffer_7_out,
       controlled_buffer_8_out, controlled_buffer_9_out, controlled_buffer_10_out, controlled_buffer_11_out,
       controlled_buffer_12_out, controlled_buffer_13_out, controlled_inverter_1_out,
       controlled_inverter_2_out, controlled_inverter_3_out, controlled_inverter_4_out, not_1_out, not_2_out,
       not_3_out, not_4_out;

  and and_1 (and_1_out, out_12, in_6);
  D_Flip_Flop d_ff_1 (
    .clk(in_5), .D(and_1_out), .Q(out_9), .preset(controlled_buffer_2_out), .reset(controlled_buffer_1_out));  // open: Qn, en
  assign controlled_buffer_1_out = in_7 ? controlled_inverter_1_out : 1'bz;  // Controlled_Buffer controlled_buffer_1
  assign controlled_buffer_2_out = in_7 ? controlled_buffer_3_out : 1'bz;  // Controlled_Buffer controlled_buffer_2
  assign controlled_inverter_1_out = not_1_out ? ~in_1 : 1'bz;  // Controlled_Inverter controlled_inverter_1
  assign controlled_buffer_3_out = in_1 ? in_1 : 1'bz;  // Controlled_Buffer controlled_buffer_3
  not not_1 (not_1_out, in_1);
  assign controlled_buffer_4_out = in_7 ? controlled_buffer_5_out : 1'bz;  // Controlled_Buffer controlled_buffer_4
  assign controlled_buffer_5_out = in_2 ? in_2 : 1'bz;  // Controlled_Buffer controlled_buffer_5
  D_Flip_Flop d_ff_2 (
    .clk(in_5), .D(out_9), .Q(out_10), .preset(controlled_buffer_4_out), .reset(controlled_buffer_6_out));  // open: Qn, en
  assign controlled_buffer_6_out = in_7 ? controlled_inverter_2_out : 1'bz;  // Controlled_Buffer controlled_buffer_6
  assign controlled_inverter_2_out = not_2_out ? ~in_2 : 1'bz;  // Controlled_Inverter controlled_inverter_2
  not not_2 (not_2_out, in_2);
  assign controlled_buffer_7_out = in_7 ? controlled_buffer_8_out : 1'bz;  // Controlled_Buffer controlled_buffer_7
  assign controlled_buffer_8_out = in_3 ? in_3 : 1'bz;  // Controlled_Buffer controlled_buffer_8
  D_Flip_Flop d_ff_3 (
    .clk(in_5), .D(out_10), .Q(out_11), .preset(controlled_buffer_7_out), .reset(controlled_buffer_9_out));  // open: Qn, en
  assign controlled_buffer_9_out = in_7 ? controlled_inverter_3_out : 1'bz;  // Controlled_Buffer controlled_buffer_9
  assign controlled_inverter_3_out = not_3_out ? ~in_3 : 1'bz;  // Controlled_Inverter controlled_inverter_3
  not not_3 (not_3_out, in_3);
  D_Flip_Flop d_ff_4 (
    .clk(in_5), .D(out_11), .Q(out_12), .preset(controlled_buffer_10_out), .reset(controlled_buffer_11_out));  // open: Qn, en
  assign controlled_buffer_10_out = in_7 ? controlled_buffer_12_out : 1'bz;  // Controlled_Buffer controlled_buffer_10
  assign controlled_buffer_11_out = in_7 ? controlled_inverter_4_out : 1'bz;  // Controlled_Buffer controlled_buffer_11
  assign controlled_inverter_4_out = not_4_out ? ~in_4 : 1'bz;  // Controlled_Inverter controlled_inverter_4
  assign controlled_buffer_12_out = in_4 ? in_4 : 1'bz;  // Controlled_Buffer controlled_buffer_12
  not not_4 (not_4_out, in_4);
  D_Flip_Flop d_ff_5 (.clk(in_5), .D(out_12), .Q(out_8), .reset(controlled_buffer_13_out));  // open: Qn, preset, en
  assign controlled_buffer_13_out = in_7 ? in_7 : 1'bz;  // Controlled_Buffer controlled_buffer_13
endmodule
